# Fritzing sketch smart_disinfection_and_sanitation_tunnel_Zkb20Q5S2B (saved by Fritzing 0.8.7b)

parts:
  Arduino_UNO = Arduino Uno (Rev3)
  Sensore_PIR_HC-SR501 = HC-SR501 Body Sensor Module
  Sensore_PIR_HC-SR502 = HC-SR501 Body Sensor Module
  KY-2 = Keyes Relay [package=THT]
  U1 = RELAY-SOLIDSTATE [package=relay-s108t02]
  Power-In_12V_(SMPS) = Power plug
  AC-In_220V = Power plug

nets:
  N1: Arduino_UNO.D12/MISO, KY-2.power
  N2: Arduino_UNO.D2, Sensore_PIR_HC-SR501.OUT
  N3: Arduino_UNO.D3_PWM, Sensore_PIR_HC-SR502.OUT
  5V: Arduino_UNO.5V, Sensore_PIR_HC-SR501.VCC, KY-2.signal
  GND: Arduino_UNO.GND, Sensore_PIR_HC-SR501.GND, KY-2.ground
  N4: KY-2.C, Power-In_12V_(SMPS).VCC
  N5: KY-2.NO, U1.+
  N6: U1.T1, AC-In_220V.VCC
  N7: U1.-, Power-In_12V_(SMPS).GND

notes:
  1HP WATER PUMP 220V
  Power Relay
  5V Relay

custom parts:
  HC-SR501 Body Sensor Module: Pyroelectric Infrared PIR Motion Sensor Detector Module
  Keyes Relay: The Keyes 5V relay module is suitable for SCM development, home appliance control. It uses a 5V~12V TIL control signal which can control DC / AC signal.
